# Fritzing sketch pico-and-io-expander (saved by Fritzing 0.9.5d)
breadboards: 1

parts:
  Pico1 = Raspberry Pi Pico
  M1 = pcf8574 io expansion board [package=THT]
  LED1 = LED - 3mm [color="Red (633nm)" package="3 mm [THT]"]

nets:
  GND: Pico1.GND, M1.GND, LED1.cathode
  3V3: Pico1.3V3, M1.VCC
  N1: Pico1.GP17, M1.SCL
  N2: Pico1.GP16, M1.SDA
  N3: M1.O1, LED1.anode

custom parts:
  Raspberry Pi Pico: Raspberry Pi Pico. Based around the RP2040 microcontroller the Pico is a low cost microcontroller device bringing Raspberry Pi quality, cost, and easy of use to the microcontroller space.
  pcf8574 io expansion board: pcf8574 io expansion board.
